# Fritzing sketch Tempsensor (saved by Fritzing 0.9.10b)
circuit board: 8cm x 5cm
breadboards: 1

parts:
  Bosch_Sensor = Barometric Pressure Sensor - BMP180 Breakout (GY-68)
  DS1 = DS18B20 1-Wire Temperature Sensor [part_number=DS18B20]
  DS2 = DS18B20 1-Wire Temperature Sensor [part_number=DS18B20]
  DS3 = DS18B20 1-Wire Temperature Sensor [part_number=DS18B20]
  R1 = Resistor [tolerance=±5% power=0.25 resistance=4700 package=THT]
  WeMos_D1_Mini1 = WeMos D1 Mini
  DS4 = DS18B20 1-Wire Temperature Sensor [part_number=DS18B20]
  DS5 = DS18B20 1-Wire Temperature Sensor [part_number=DS18B20]

nets:
  VDD: Bosch_Sensor.VCC, DS1.VDD, DS2.VDD, DS3.VDD, R1.Pin_0, WeMos_D1_Mini1.3V3, DS4.VDD, DS5.VDD
  GND: Bosch_Sensor.GND, DS1.GND, DS2.GND, DS3.GND, WeMos_D1_Mini1.G, DS4.GND, DS5.GND
  N1: Bosch_Sensor.SCL, WeMos_D1_Mini1.D5
  N2: Bosch_Sensor.SDA, WeMos_D1_Mini1.D6
  N3: DS1.DQ, DS2.DQ, DS3.DQ, R1.Pin_1, WeMos_D1_Mini1.D7, DS4.DQ, DS5.DQ

notes:
  Till Dettmering 2022
